# Fritzing sketch projeto (saved by Fritzing 0.9.3b)
breadboards: 1

parts:
  Componente2 = Arduino Uno (Rev3)
  RHT3 = Humidity and Temperature Sensor RHT03 [part_number=DHT22]
  LED3 = RGB LED (com. cathode, rgb) [package="5 mm [THT]"]
  R8 = Resistor [tolerance=±5% resistance=220 package=THT]
  R9 = Rotary Potentiometer (Large) [maximum_resistance=100kΩ package=THT]
  R10 = Resistor [tolerance=±5% resistance=220 package=THT]
  J1 = Basic Servo

nets:
  N1: Componente2.A5/SCL, R9.wiper
  N2: Componente2.D8, RHT3.Data-signal, R8.Pin_0
  N3: Componente2.D9_PWM, LED3.red_anode
  N4: Componente2.D10_PWM/SS, LED3.green_anode
  N5: Componente2.D11_PWM/MOSI, LED3.blue_anode
  VCC: Componente2.5V, RHT3.Vcc, R8.Pin_1, R9.leg1, J1.vcc
  GND: Componente2.GND, RHT3.GND_2, R9.leg2, R10.Pin_1, J1.gnd
  N6: LED3.common_cathode, R10.Pin_0
